# Fritzing sketch calculator (saved by Fritzing 0.9.5d)
breadboards: 1

parts:
  Part2 = Arduino Uno (Rev3) - ICSP
  U1 = LCD-16X2 [package=lcd-16x2]
  R1 = Resistor [tolerance=±5% resistance=220 package="0603 [SMD]"]
  R2 = Trimmer Potentiometer [maximum_resistance=10kΩ package=THT]
  R3 = Trimmer Potentiometer [maximum_resistance=10kΩ package=THT]
  R4 = Trimmer Potentiometer [maximum_resistance=10kΩ package=THT]
  J1 = Piezo Speaker
  S1 = Momentary Switch [package=ksa_sealed_tac_switch]
  S2 = Momentary Switch [package=ksa_sealed_tac_switch]
  S3 = Momentary Switch [package=ksa_sealed_tac_switch]

nets:
  N1: Part2.A0, R2.wiper
  N2: Part2.A1, R3.wiper
  5V: Part2.5V, U1.VDD, R1.Pin_0, R2.leg2, R3.leg2, R4.leg1, J1.pin1
  N3: Part2.D8, S3.3, S3.4
  N4: Part2.D9_PWM, S1.1, S1.2
  N5: Part2.D11_PWM/MOSI, U1.RS
  N6: Part2.D12/MISO, U1.E
  N7: Part2.D13/SCK, S2.3, S2.4
  GND: Part2.GND, U1.VSS, U1.R_W, U1.K, R2.leg1, R3.leg1, R4.leg2, S1.3, S1.4, S2.1, S2.2, S3.1, S3.2
  N8: Part2.D2, U1.DB4
  N9: Part2.D3_PWM, U1.DB5
  N10: Part2.D4, U1.DB6
  N11: Part2.D5_PWM, U1.DB7
  N12: Part2.D7, J1.pin2
  N13: U1.VO, R4.wiper
  N14: U1.A, R1.Pin_1
